# Fritzing sketch Maket (saved by Fritzing 0.9.3b)

parts:
  Часть1 = Arduino Nano (Rev3.0)
  Q2 = Basic FET N-Channel [package="DPak [SMD]"]
  Q3 = Basic FET N-Channel [package="DPak [SMD]"]
  Q5 = Basic FET N-Channel [package="DPak [SMD]"]
  R1 = Resistor [tolerance=±5% resistance=220 package=THT]
  R2 = Resistor [tolerance=±5% resistance=220 package=THT]
  R3 = Resistor [tolerance=±5% resistance=220 package=THT]
  Power_plug1 = Power plug
  Q6 = Basic FET N-Channel [package="DPak [SMD]"]
  R4 = Resistor [tolerance=±5% resistance=220 package=THT]
  R5 = Resistor [tolerance=±5% resistance=220 package=THT]
  R6 = Resistor [tolerance=±5% resistance=220 package=THT]
  R7 = Resistor [tolerance=±5% resistance=220 package=THT]
  R8 = Resistor [tolerance=±5% resistance=220 package=THT]
  LED1 = LED - 5mm [color="Red (633nm)" package="5 mm [THT]"]
  LED2 = LED - 5mm [color="Red (633nm)" package="5 mm [THT]"]
  LED3 = LED - 5mm [color="Red (633nm)" package="5 mm [THT]"]
  LED4 = LED - 5mm [color="Red (633nm)" package="5 mm [THT]"]
  S1 = Pushbutton [package="[THT]"]
  S2 = Pushbutton [package="[THT]"]
  S3 = Pushbutton [package="[THT]"]
  S4 = Pushbutton [package="[THT]"]
  S5 = Toggle Switch [package=THT]
  S6 = Pushbutton [package="[THT]"]

nets (from the breadboard view):
  GND: Часть1.GND, Q2.source, Q3.source, Q5.source, R1.Pin_1, R2.Pin_1, R3.Pin_1, Power_plug1.GND, Q6.source, R4.Pin_1, S5.COM, S6.Pin_1, S6.Pin_2
  N1: Часть1.D2, S6.Pin_3, S6.Pin_4
  N2: Часть1.D4, S5.L1
  N3: Часть1.D5, R5.Pin_0
  N4: Часть1.D6, R6.Pin_0
  N5: Часть1.D7, R7.Pin_0
  N6: Часть1.D8, R8.Pin_0
  N7: Часть1.D9, S1.Pin_3, S1.Pin_4
  N8: Часть1.D10, S2.Pin_3
  N9: Часть1.D11/MOSI, S3.Pin_3, S3.Pin_4
  N10: Часть1.D12/MISO, S4.Pin_3, S4.Pin_4
  VIN: Часть1.VIN, Power_plug1.VCC, LED1.cathode, LED2.cathode, LED3.cathode, LED4.cathode
  N11: Q2.Gate, R3.Pin_0, R6.Pin_1
  N12: Q2.drain, LED1.anode, S2.Pin_1, S2.Pin_2
  N13: Q3.Gate, R2.Pin_0, R5.Pin_1
  N14: Q3.drain, LED4.anode, S1.Pin_2
  N15: Q5.Gate, R1.Pin_0, R7.Pin_1
  N16: Q5.drain, LED2.anode, S3.Pin_2
  N17: Q6.Gate, R4.Pin_0, R8.Pin_1
  N18: Q6.drain, LED3.anode, S4.Pin_2
